// Logisim project part1.circ as structural Verilog: 1 circuit, main circuit main
module main (
  input  D,
  input  Clk,
  output nQ,
  output Q
);

  wire n7400_1_p3, n7400_1_p6, n7400_2_p3;

  // _7400 7400_1: pin names not known; wires that end beside it: D, D, n7400_1_p3, n7400_1_p3, Clk, n7400_1_p6
  // _7400 7400_2: pin names not known; wires that end beside it: D, Clk, n7400_2_p3, n7400_2_p3, nQ, Q, n7400_1_p6, Q, nQ
endmodule
